// Logisim project AND gate.circ as structural Verilog: 1 circuit, main circuit main
module main (
  input  in_1,
  input  in_2,
  output out_3
);

  wire AND_out;

  nand AND (AND_out, in_1, in_2);
  not Not (out_3, AND_out);
endmodule
