// Logisim project AND16.circ as structural Verilog: 1 circuit, main circuit main
module main (
  input  [15:0] in_1,
  input  [15:0] in_2,
  input  [15:0] in_3,
  input  [15:0] in_4,
  output [15:0] out_5,
  output [15:0] out_6
);

  assign out_5 = in_1 & in_2;  // AND_Gate AND, 16 bits wide
  and AND_2 (out_6[0], in_3[0], in_4[0]);
  and AND_3 (out_6[1], in_3[1], in_4[1]);
  and AND_4 (out_6[2], in_3[2], in_4[2]);
  and AND_5 (out_6[3], in_3[3], in_4[3]);
  and AND_6 (out_6[4], in_3[4], in_4[4]);
  and AND_7 (out_6[5], in_3[5], in_4[5]);
  and AND_8 (out_6[6], in_3[6], in_4[6]);
  and AND_9 (out_6[7], in_3[7], in_4[7]);
  and AND_10 (out_6[8], in_3[8], in_4[8]);
  and AND_11 (out_6[9], in_3[9], in_4[9]);
  and AND_12 (out_6[10], in_3[10], in_4[10]);
  and AND_13 (out_6[11], in_3[11], in_4[11]);
  and AND_14 (out_6[12], in_3[12], in_4[12]);
  and AND_15 (out_6[13], in_3[13], in_4[13]);
  and AND_16 (out_6[14], in_3[14], in_4[14]);
  and AND_17 (out_6[15], in_3[15], in_4[15]);

  // Notes on the sheet:
  //   A[16]
  //   B[16]
  //   INPUTS
  //   A[16]
  //   SPLITTER
  //   B[16]
  //   OUTPUT [16]
  //   SPLITTER
  //   OUTPUT[16]
endmodule
