// Logisim project Add16.circ as structural Verilog: 1 circuit, main circuit main
module main (
  input  in_1,
  input  [15:0] in_2,
  input  [15:0] in_3,
  input  CARRY_IN___0,
  input  [15:0] in_5,
  input  [15:0] in_6,
  output [15:0] out_7,
  output CARRY_OUT,
  output [15:0] out_9,
  output out_10
);

  wire adder_2_cout, adder_3_cout, adder_4_cout, adder_5_cout, adder_6_cout, adder_7_cout, adder_8_cout,
       adder_9_cout, adder_10_cout, adder_11_cout, adder_12_cout, adder_13_cout, adder_14_cout,
       adder_15_cout, adder_16_cout;

  Adder #(.width(16)) adder_1 (.a(in_3), .b(in_5), .out(out_7), .cin(CARRY_IN___0), .cout(CARRY_OUT));
  Adder #(.width(1)) adder_2 (.a(in_2[0]), .b(in_6[0]), .out(out_9[0]), .cin(in_1), .cout(adder_2_cout));
  Adder #(.width(1)) adder_3 (.a(in_2[1]), .b(in_6[1]), .out(out_9[1]), .cin(adder_2_cout), .cout(adder_3_cout));
  Adder #(.width(1)) adder_4 (.a(in_2[2]), .b(in_6[2]), .out(out_9[2]), .cin(adder_3_cout), .cout(adder_4_cout));
  Adder #(.width(1)) adder_5 (.a(in_2[3]), .b(in_6[3]), .out(out_9[3]), .cin(adder_4_cout), .cout(adder_5_cout));
  Adder #(.width(1)) adder_6 (.a(in_2[4]), .b(in_6[4]), .out(out_9[4]), .cin(adder_5_cout), .cout(adder_6_cout));
  Adder #(.width(1)) adder_7 (.a(in_2[5]), .b(in_6[5]), .out(out_9[5]), .cin(adder_6_cout), .cout(adder_7_cout));
  Adder #(.width(1)) adder_8 (.a(in_2[6]), .b(in_6[6]), .out(out_9[6]), .cin(adder_7_cout), .cout(adder_8_cout));
  Adder #(.width(1)) adder_9 (.a(in_2[7]), .b(in_6[7]), .out(out_9[7]), .cin(adder_8_cout), .cout(adder_9_cout));
  Adder #(.width(1)) adder_10 (.a(in_2[8]), .b(in_6[8]), .out(out_9[8]), .cin(adder_9_cout), .cout(adder_10_cout));
  Adder #(.width(1)) adder_11 (.a(in_2[9]), .b(in_6[9]), .out(out_9[9]), .cin(adder_10_cout), .cout(adder_11_cout));
  Adder #(.width(1)) adder_12 (.a(in_2[10]), .b(in_6[10]), .out(out_9[10]), .cin(adder_11_cout), .cout(adder_12_cout));
  Adder #(.width(1)) adder_13 (.a(in_2[11]), .b(in_6[11]), .out(out_9[11]), .cin(adder_12_cout), .cout(adder_13_cout));
  Adder #(.width(1)) adder_14 (.a(in_2[12]), .b(in_6[12]), .out(out_9[12]), .cin(adder_13_cout), .cout(adder_14_cout));
  Adder #(.width(1)) adder_15 (.a(in_6[13]), .b(in_2[13]), .out(out_9[13]), .cin(adder_14_cout), .cout(adder_15_cout));
  Adder #(.width(1)) adder_16 (.a(in_2[14]), .b(in_6[14]), .out(out_9[14]), .cin(adder_15_cout), .cout(adder_16_cout));
  Adder #(.width(1)) adder_17 (.a(in_2[15]), .b(in_6[15]), .out(out_9[15]), .cin(adder_16_cout), .cout(out_10));

  // Notes on the sheet:
  //   A[16]
  //   B[16]
  //   A[16]
  //   B[16]
  //   OUTPUT [16]
endmodule
