// Logisim project DFF con Mux.circ as structural Verilog: 2 circuits, main circuit bit
module \bit  (
  input  clock,
  input  in_2,
  input  in_3,
  output out_4
);

  wire multiplexer_1_out;

  Multiplexer #(.enable("false")) multiplexer_1 (.in0(out_4), .in1(in_2), .out(multiplexer_1_out), .sel(in_3));
  D_Flip_Flop d_ff_1 (.clk(clock), .D(multiplexer_1_out), .Q(out_4));  // open: Qn, preset, en, reset
endmodule

module Registro (
  input  [15:0] in_1,
  input  in_2,
  output [15:0] out_3
);

  wire clock_1_out;

  Clock clock_1 (.out(clock_1_out));
  \bit  bit_1 (.clock(clock_1_out), .in_2(in_1[0]), .in_3(in_2), .out_4(out_3[0]));
  \bit  bit_2 (.clock(clock_1_out), .in_2(in_1[1]), .in_3(in_2), .out_4(out_3[1]));
  \bit  bit_3 (.clock(clock_1_out), .in_2(in_1[2]), .in_3(in_2), .out_4(out_3[2]));
  \bit  bit_4 (.clock(clock_1_out), .in_2(in_1[3]), .in_3(in_2), .out_4(out_3[3]));
  \bit  bit_5 (.clock(clock_1_out), .in_2(in_1[4]), .in_3(in_2), .out_4(out_3[4]));
  \bit  bit_6 (.clock(clock_1_out), .in_2(in_1[5]), .in_3(in_2), .out_4(out_3[5]));
  \bit  bit_7 (.clock(clock_1_out), .in_2(in_1[6]), .in_3(in_2), .out_4(out_3[6]));
  \bit  bit_8 (.clock(clock_1_out), .in_2(in_1[7]), .in_3(in_2), .out_4(out_3[7]));
  \bit  bit_9 (.clock(clock_1_out), .in_2(in_1[8]), .in_3(in_2), .out_4(out_3[8]));
  \bit  bit_10 (.clock(clock_1_out), .in_2(in_1[9]), .in_3(in_2), .out_4(out_3[9]));
  \bit  bit_11 (.clock(clock_1_out), .in_2(in_1[10]), .in_3(in_2), .out_4(out_3[10]));
  \bit  bit_12 (.clock(clock_1_out), .in_2(in_1[11]), .in_3(in_2), .out_4(out_3[11]));
  \bit  bit_13 (.clock(clock_1_out), .in_2(in_1[12]), .in_3(in_2), .out_4(out_3[12]));
  \bit  bit_14 (.clock(clock_1_out), .in_2(in_1[13]), .in_3(in_2), .out_4(out_3[13]));
  \bit  bit_15 (.clock(clock_1_out), .in_2(in_1[14]), .in_3(in_2), .out_4(out_3[14]));
  \bit  bit_16 (.clock(clock_1_out), .in_2(in_1[15]), .in_3(in_2), .out_4(out_3[15]));

  // Other names for the same wires on the sheet: load = in_2
endmodule
