// Logisim project DMUX4WAY.circ as structural Verilog: 1 circuit, main circuit main
module main (
  input  IN,
  input  [1:0] SEL_2,
  output A,
  output B,
  output C,
  output D
);

  wire demultiplexer_1_out0, demultiplexer_1_out1;

  Demultiplexer demultiplexer_1 (
    .out0(demultiplexer_1_out0), .out1(demultiplexer_1_out1), .in(IN), .sel(SEL_2[0]));  // open: en
  Demultiplexer demultiplexer_2 (.out0(A), .out1(B), .in(demultiplexer_1_out0), .sel(SEL_2[1]));  // open: en
  Demultiplexer demultiplexer_3 (.out0(C), .out1(D), .in(demultiplexer_1_out1), .sel(SEL_2[1]));  // open: en

  // Notes on the sheet:
  //   SEL[0]
  //   SPLITTER
  //   SEL[1]
endmodule
