// Logisim project DMUX8WAY.circ as structural Verilog: 1 circuit, main circuit main
module main (
  input  IN,
  input  [2:0] SEL_3,
  output A,
  output B,
  output C,
  output D,
  output E,
  output F,
  output G,
  output H
);

  wire demultiplexer_1_out0, demultiplexer_1_out1, demultiplexer_2_out0, demultiplexer_2_out1,
       demultiplexer_3_out0, demultiplexer_3_out1;

  Demultiplexer demultiplexer_1 (
    .out0(demultiplexer_1_out0), .out1(demultiplexer_1_out1), .in(IN), .sel(SEL_3[2]));  // open: en
  Demultiplexer demultiplexer_2 (
    .out0(demultiplexer_2_out0), .out1(demultiplexer_2_out1), .in(demultiplexer_1_out0), .sel(SEL_3[1]));  // open: en
  Demultiplexer demultiplexer_3 (
    .out0(demultiplexer_3_out0), .out1(demultiplexer_3_out1), .in(demultiplexer_1_out1), .sel(SEL_3[1]));  // open: en
  Demultiplexer demultiplexer_4 (.out0(A), .out1(B), .in(demultiplexer_2_out0), .sel(SEL_3[0]));  // open: en
  Demultiplexer demultiplexer_5 (.out0(C), .out1(D), .in(demultiplexer_2_out1), .sel(SEL_3[0]));  // open: en
  Demultiplexer demultiplexer_6 (.out0(E), .out1(F), .in(demultiplexer_3_out0), .sel(SEL_3[0]));  // open: en
  Demultiplexer demultiplexer_7 (.out0(G), .out1(H), .in(demultiplexer_3_out1), .sel(SEL_3[0]));  // open: en

  // Notes on the sheet:
  //   SEL[0]
  //   SEL[1]
  //   SEL[2]
  //   SEL[2]
endmodule
