// Logisim project DMux chip.circ as structural Verilog: 1 circuit, main circuit main
module main (
  input  a,
  input  Sel,
  output out_3,
  output out_4
);

  wire Not_out;

  not Not (Not_out, Sel);
  nand AND (out_3, a, Not_out);
  nand AND_2 (out_4, Sel, a);
endmodule
