// Logisim project Full adder chip.circ as structural Verilog: 1 circuit, main circuit main
module main (
  input  a,
  input  b,
  input  in_3,
  output sum,
  output Cout
);

  wire and_2_out, AND_out, XOR_out;

  xor XOR (XOR_out, a, b);
  and AND (AND_out, a, b);
  and and_2 (and_2_out, XOR_out, in_3);
  xor xor_2 (sum, XOR_out, in_3);
  xor xor_3 (Cout, and_2_out, AND_out);
endmodule
