// Logisim project MUX8WAY16.circ as structural Verilog: 1 circuit, main circuit main
module main (
  input  [15:0] in_1,
  input  [15:0] in_2,
  input  [15:0] in_3,
  input  [15:0] in_4,
  input  [2:0] SEL_3,
  input  [15:0] in_6,
  input  [15:0] in_7,
  input  [15:0] in_8,
  input  [15:0] in_9,
  output [15:0] out_10
);

  wire [15:0] multiplexer_1_out, multiplexer_2_out, multiplexer_3_out, multiplexer_4_out, multiplexer_5_out,
       multiplexer_6_out;

  Multiplexer #(.width(16)) multiplexer_1 (
    .in0(in_1), .in1(in_2), .out(multiplexer_1_out), .sel(SEL_3[0]));  // open: en
  Multiplexer #(.width(16)) multiplexer_2 (
    .in0(in_3), .in1(in_4), .out(multiplexer_2_out), .sel(SEL_3[0]));  // open: en
  Multiplexer #(.width(16)) multiplexer_3 (
    .in0(in_6), .in1(in_7), .out(multiplexer_3_out), .sel(SEL_3[0]));  // open: en
  Multiplexer #(.width(16)) multiplexer_4 (
    .in0(in_8), .in1(in_9), .out(multiplexer_4_out), .sel(SEL_3[0]));  // open: en
  Multiplexer #(.width(16)) multiplexer_5 (
    .in0(multiplexer_1_out), .in1(multiplexer_2_out), .out(multiplexer_5_out), .sel(SEL_3[1]));  // open: en
  Multiplexer #(.width(16)) multiplexer_6 (
    .in0(multiplexer_3_out), .in1(multiplexer_4_out), .out(multiplexer_6_out), .sel(SEL_3[1]));  // open: en
  Multiplexer #(.width(16)) multiplexer_7 (
    .in0(multiplexer_5_out), .in1(multiplexer_6_out), .out(out_10), .sel(SEL_3[2]));  // open: en

  // Notes on the sheet:
  //   SPLITTER
  //   A[16]
  //   B[16]
  //   C[16]
  //   D[16]
  //   E[16]
  //   F[16]
  //   G[16]
  //   H[16]
  //   SEL[0]
  //   SEL[0]
  //   SEL[1]
  //   SEL[2]
  //   OUTPUT[16]
endmodule
