// Logisim project Multiplexor.circ as structural Verilog: 1 circuit, main circuit main
module main (
  input  a,
  input  sel,
  input  b
);

  wire and_1_out, not_1_out, not_3_out;

  not not_1 (not_1_out, a);
  // NOT_Gate not_2 has open pins: in=sel, out=open
  not not_3 (not_3_out, b);
  and and_1 (and_1_out, not_1_out, b);
  // AND_Gate and_2 has open pins: in0=and_1_out, in1=sel, out=open
  // AND_Gate and_3 has open pins: in0=a, in1=not_3_out, out=open
  // AND_Gate and_4 is placed but not wired
endmodule
