// Logisim project Mux chip.circ as structural Verilog: 1 circuit, main circuit main
module main (
  input  a,
  input  Sel,
  input  b,
  output out_4
);

  wire AND_2_out, AND_out, Not_out;

  not Not (Not_out, Sel);
  nand AND (AND_out, a, Sel);
  nand AND_2 (AND_2_out, Not_out, b);
  or Or (out_4, AND_out, AND_2_out);
endmodule
