// Logisim project Or gate.circ as structural Verilog: 1 circuit, main circuit main
module main (
  input  in_1,
  input  in_2,
  output out_3
);

  wire Not_2_out, Not_out;

  not Not (Not_out, in_1);
  not Not_2 (Not_2_out, in_2);
  nand AND (out_3, Not_out, Not_2_out);
endmodule
