// Logisim project Or16.circ as structural Verilog: 1 circuit, main circuit main
module main (
  input  [15:0] in_1,
  input  [15:0] in_2,
  output [15:0] out_3
);

  wire [15:0] Not_2_out, Not_out;

  assign Not_out = ~in_1;  // NOT_Gate Not, 16 bits wide
  assign Not_2_out = ~in_2;  // NOT_Gate Not_2, 16 bits wide
  assign out_3 = ~(Not_out & Not_2_out);  // NAND_Gate AND, 16 bits wide
endmodule
