// Logisim project Or8Way.circ as structural Verilog: 1 circuit, main circuit main
module main (
  input  In,
  input  In_2,
  input  In_3,
  input  In_4,
  input  In_5,
  input  In_6,
  input  In_7,
  input  In_8,
  output out_9
);

  wire Or_2_out, Or_3_out, Or_4_out, Or_5_out, Or_6_out, Or_out;

  or Or (Or_out, In, In_2);
  or Or_2 (Or_2_out, In_3, In_4);
  or Or_3 (Or_3_out, In_5, In_6);
  or Or_4 (Or_4_out, In_7, In_8);
  or Or_5 (Or_5_out, Or_out, Or_2_out);
  or Or_6 (Or_6_out, Or_3_out, Or_4_out);
  or Or_7 (out_9, Or_5_out, Or_6_out);
endmodule
