// Logisim project RAM512.circ as structural Verilog: 1 circuit, main circuit main
module main (
  input  clock,
  input  [15:0] in,
  input  load,
  input  [8:0] address,
  output [15:0] out
);

  wire demultiplexer_1_out0, demultiplexer_1_out1, demultiplexer_1_out2, demultiplexer_1_out3,
       demultiplexer_1_out4, demultiplexer_1_out5, demultiplexer_1_out6, demultiplexer_1_out7;
  wire [15:0] _0RAM64_out, _1RAM64_out, _2RAM64_out, _3RAM64_out, _4RAM64_out, _5RAM64_out, _6RAM64_out,
       _7RAM64_out;

  Demultiplexer #(.select(3), .enable("false")) demultiplexer_1 (
    .out0(demultiplexer_1_out0), .out1(demultiplexer_1_out1), .out2(demultiplexer_1_out2),
    .out3(demultiplexer_1_out3), .out4(demultiplexer_1_out4), .out5(demultiplexer_1_out5),
    .out6(demultiplexer_1_out6), .out7(demultiplexer_1_out7), .in(load), .sel(address[8:6]));
  RAM64 _0RAM64 (.clock(clock), .a(in), .load(demultiplexer_1_out0), .address(address[5:0]), .out(_0RAM64_out));
  RAM64 _1RAM64 (.clock(clock), .a(in), .load(demultiplexer_1_out1), .address(address[5:0]), .out(_1RAM64_out));
  RAM64 _2RAM64 (.clock(clock), .a(in), .load(demultiplexer_1_out2), .address(address[5:0]), .out(_2RAM64_out));
  RAM64 _3RAM64 (.clock(clock), .a(in), .load(demultiplexer_1_out3), .address(address[5:0]), .out(_3RAM64_out));
  RAM64 _4RAM64 (.clock(clock), .a(in), .load(demultiplexer_1_out4), .address(address[5:0]), .out(_4RAM64_out));
  RAM64 _5RAM64 (.clock(clock), .a(in), .load(demultiplexer_1_out5), .address(address[5:0]), .out(_5RAM64_out));
  RAM64 _6RAM64 (.clock(clock), .a(in), .load(demultiplexer_1_out6), .address(address[5:0]), .out(_6RAM64_out));
  RAM64 _7RAM64 (.clock(clock), .a(in), .load(demultiplexer_1_out7), .address(address[5:0]), .out(_7RAM64_out));
  Multiplexer #(.select(3), .width(16), .enable("false")) multiplexer_1 (
    .in0(_0RAM64_out), .in1(_1RAM64_out), .in2(_2RAM64_out), .in3(_3RAM64_out), .in4(_4RAM64_out),
    .in5(_5RAM64_out), .in6(_6RAM64_out), .in7(_7RAM64_out), .out(out), .sel(address[8:6]));

  // Notes on the sheet:
  //   ADDRESS
  //   - 3 para decidir en CUÁL chip guardar
  //   000 -> 	RAM 0
  //   001 -> 	RAM 1
  //   010 -> 	RAM 2
  //   011 -> 	RAM 3
  //   100 -> 	RAM 4
  //   101 -> 	RAM 5
  //   110 -> 	RAM 6
  //   111 -> 	RAM 7
  //   - 6 para elegir QUÉ REGISTRO dentro de ese chip usar.
endmodule
