// Logisim project RAM64.circ as structural Verilog: 2 circuits, main circuit RAM64
module RAM64 (
  input  clock,
  input  [15:0] a,
  input  load,
  input  [5:0] address,
  output [15:0] out
);

  wire demultiplexer_1_out0, demultiplexer_1_out1, demultiplexer_1_out2, demultiplexer_1_out3,
       demultiplexer_1_out4, demultiplexer_1_out5, demultiplexer_1_out6, demultiplexer_1_out7;
  wire [15:0] _0RAM8_out, _1RAM8_out, _2RAM8_out, _3RAM8_out, _4RAM8_out, _5RAM8_out, _6RAM8_out, _7RAM8_out;

  Demultiplexer #(.select(3), .enable("false")) demultiplexer_1 (
    .out0(demultiplexer_1_out0), .out1(demultiplexer_1_out1), .out2(demultiplexer_1_out2),
    .out3(demultiplexer_1_out3), .out4(demultiplexer_1_out4), .out5(demultiplexer_1_out5),
    .out6(demultiplexer_1_out6), .out7(demultiplexer_1_out7), .in(load), .sel(address[5:3]));
  RAM8 _0RAM8 (.Clock(clock), .in(a), .load(demultiplexer_1_out0), .address(address[2:0]), .out(_0RAM8_out));
  RAM8 _1RAM8 (.Clock(clock), .in(a), .load(demultiplexer_1_out1), .address(address[2:0]), .out(_1RAM8_out));
  RAM8 _2RAM8 (.Clock(clock), .in(a), .load(demultiplexer_1_out2), .address(address[2:0]), .out(_2RAM8_out));
  RAM8 _3RAM8 (.Clock(clock), .in(a), .load(demultiplexer_1_out3), .address(address[2:0]), .out(_3RAM8_out));
  RAM8 _4RAM8 (.Clock(clock), .in(a), .load(demultiplexer_1_out4), .address(address[2:0]), .out(_4RAM8_out));
  RAM8 _5RAM8 (.Clock(clock), .in(a), .load(demultiplexer_1_out5), .address(address[2:0]), .out(_5RAM8_out));
  RAM8 _6RAM8 (.Clock(clock), .in(a), .load(demultiplexer_1_out6), .address(address[2:0]), .out(_6RAM8_out));
  RAM8 _7RAM8 (.Clock(clock), .in(a), .load(demultiplexer_1_out7), .address(address[2:0]), .out(_7RAM8_out));
  Multiplexer #(.select(3), .width(16), .enable("false")) multiplexer_1 (
    .in0(_0RAM8_out), .in1(_1RAM8_out), .in2(_2RAM8_out), .in3(_3RAM8_out), .in4(_4RAM8_out),
    .in5(_5RAM8_out), .in6(_6RAM8_out), .in7(_7RAM8_out), .out(out), .sel(address[5:3]));
endmodule

module RAM64_clock (
  input  [15:0] a,
  input  load,
  input  [5:0] address,
  output [15:0] out
);

  wire clock_1_out, demultiplexer_1_out0, demultiplexer_1_out1, demultiplexer_1_out2, demultiplexer_1_out3,
       demultiplexer_1_out4, demultiplexer_1_out5, demultiplexer_1_out6, demultiplexer_1_out7;
  wire [15:0] _0RAM8_out, _1RAM8_out, _2RAM8_out, _3RAM8_out, _4RAM8_out, _5RAM8_out, _6RAM8_out, _7RAM8_out;

  Demultiplexer #(.select(3), .enable("false")) demultiplexer_1 (
    .out0(demultiplexer_1_out0), .out1(demultiplexer_1_out1), .out2(demultiplexer_1_out2),
    .out3(demultiplexer_1_out3), .out4(demultiplexer_1_out4), .out5(demultiplexer_1_out5),
    .out6(demultiplexer_1_out6), .out7(demultiplexer_1_out7), .in(load), .sel(address[5:3]));
  Clock clock_1 (.out(clock_1_out));
  RAM8 _0RAM8 (.Clock(clock_1_out), .in(a), .load(demultiplexer_1_out0), .address(address[2:0]), .out(_0RAM8_out));
  RAM8 _1RAM8 (.Clock(clock_1_out), .in(a), .load(demultiplexer_1_out1), .address(address[2:0]), .out(_1RAM8_out));
  RAM8 _2RAM8 (.Clock(clock_1_out), .in(a), .load(demultiplexer_1_out2), .address(address[2:0]), .out(_2RAM8_out));
  RAM8 _3RAM8 (.Clock(clock_1_out), .in(a), .load(demultiplexer_1_out3), .address(address[2:0]), .out(_3RAM8_out));
  RAM8 _4RAM8 (.Clock(clock_1_out), .in(a), .load(demultiplexer_1_out4), .address(address[2:0]), .out(_4RAM8_out));
  RAM8 _5RAM8 (.Clock(clock_1_out), .in(a), .load(demultiplexer_1_out5), .address(address[2:0]), .out(_5RAM8_out));
  RAM8 _6RAM8 (.Clock(clock_1_out), .in(a), .load(demultiplexer_1_out6), .address(address[2:0]), .out(_6RAM8_out));
  RAM8 _7RAM8 (.Clock(clock_1_out), .in(a), .load(demultiplexer_1_out7), .address(address[2:0]), .out(_7RAM8_out));
  Multiplexer #(.select(3), .width(16), .enable("false")) multiplexer_1 (
    .in0(_0RAM8_out), .in1(_1RAM8_out), .in2(_2RAM8_out), .in3(_3RAM8_out), .in4(_4RAM8_out),
    .in5(_5RAM8_out), .in6(_6RAM8_out), .in7(_7RAM8_out), .out(out), .sel(address[5:3]));
endmodule
