// Logisim project RAM8.circ as structural Verilog: 1 circuit, main circuit RAM8
module RAM8 (
  input  Clock,
  input  [15:0] in,
  input  load,
  input  [2:0] address,
  output [15:0] out
);

  wire demultiplexer_1_out0, demultiplexer_1_out1, demultiplexer_1_out2, demultiplexer_1_out3,
       demultiplexer_1_out4, demultiplexer_1_out5, demultiplexer_1_out6, demultiplexer_1_out7;
  wire [15:0] Reg0_out, Reg1_out, Reg2_out, Reg3_out, Reg4_out, Reg5_out, Reg6_out, Reg7_out;

  Demultiplexer #(.select(3), .enable("false")) demultiplexer_1 (
    .out0(demultiplexer_1_out0), .out1(demultiplexer_1_out1), .out2(demultiplexer_1_out2),
    .out3(demultiplexer_1_out3), .out4(demultiplexer_1_out4), .out5(demultiplexer_1_out5),
    .out6(demultiplexer_1_out6), .out7(demultiplexer_1_out7), .in(load), .sel(address));
  Registro Reg0 (.In(in), .Clock(Clock), .load(demultiplexer_1_out0), .Out(Reg0_out));
  Registro Reg1 (.In(in), .Clock(Clock), .load(demultiplexer_1_out1), .Out(Reg1_out));
  Registro Reg2 (.In(in), .Clock(Clock), .load(demultiplexer_1_out2), .Out(Reg2_out));
  Registro Reg3 (.In(in), .Clock(Clock), .load(demultiplexer_1_out3), .Out(Reg3_out));
  Registro Reg4 (.In(in), .Clock(Clock), .load(demultiplexer_1_out4), .Out(Reg4_out));
  Registro Reg5 (.In(in), .Clock(Clock), .load(demultiplexer_1_out5), .Out(Reg5_out));
  Registro Reg6 (.In(in), .Clock(Clock), .load(demultiplexer_1_out6), .Out(Reg6_out));
  Registro Reg7 (.In(in), .Clock(Clock), .load(demultiplexer_1_out7), .Out(Reg7_out));
  Multiplexer #(.select(3), .width(16), .enable("false")) multiplexer_1 (
    .in0(Reg0_out), .in1(Reg1_out), .in2(Reg2_out), .in3(Reg3_out), .in4(Reg4_out), .in5(Reg5_out),
    .in6(Reg6_out), .in7(Reg7_out), .out(out), .sel(address));
endmodule
