// Logisim project REGISTRO.circ as structural Verilog: 2 circuits, main circuit bit
module \bit  (
  input  clock,
  input  in_2,
  input  in_3,
  output out_4
);

  wire multiplexer_1_out;

  Multiplexer #(.enable("false")) multiplexer_1 (.in0(out_4), .in1(in_2), .out(multiplexer_1_out), .sel(in_3));
  D_Flip_Flop d_ff_1 (.clk(clock), .D(multiplexer_1_out), .Q(out_4));  // open: Qn, preset, en, reset
endmodule

module Registro (
  input  [15:0] In,
  input  Clock,
  input  load,
  output [15:0] Out
);

  \bit  bit_1 (.clock(Clock), .in_2(In[0]), .in_3(load), .out_4(Out[0]));
  \bit  bit_2 (.clock(Clock), .in_2(In[1]), .in_3(load), .out_4(Out[1]));
  \bit  bit_3 (.clock(Clock), .in_2(In[2]), .in_3(load), .out_4(Out[2]));
  \bit  bit_4 (.clock(Clock), .in_2(In[3]), .in_3(load), .out_4(Out[3]));
  \bit  bit_5 (.clock(Clock), .in_2(In[4]), .in_3(load), .out_4(Out[4]));
  \bit  bit_6 (.clock(Clock), .in_2(In[5]), .in_3(load), .out_4(Out[5]));
  \bit  bit_7 (.clock(Clock), .in_2(In[6]), .in_3(load), .out_4(Out[6]));
  \bit  bit_8 (.clock(Clock), .in_2(In[7]), .in_3(load), .out_4(Out[7]));
  \bit  bit_9 (.clock(Clock), .in_2(In[8]), .in_3(load), .out_4(Out[8]));
  \bit  bit_10 (.clock(Clock), .in_2(In[9]), .in_3(load), .out_4(Out[9]));
  \bit  bit_11 (.clock(Clock), .in_2(In[10]), .in_3(load), .out_4(Out[10]));
  \bit  bit_12 (.clock(Clock), .in_2(In[11]), .in_3(load), .out_4(Out[11]));
  \bit  bit_13 (.clock(Clock), .in_2(In[12]), .in_3(load), .out_4(Out[12]));
  \bit  bit_14 (.clock(Clock), .in_2(In[13]), .in_3(load), .out_4(Out[13]));
  \bit  bit_15 (.clock(Clock), .in_2(In[14]), .in_3(load), .out_4(Out[14]));
  \bit  bit_16 (.clock(Clock), .in_2(In[15]), .in_3(load), .out_4(Out[15]));
endmodule
