// Logisim project Sumador binario parcial.circ as structural Verilog: 1 circuit, main circuit main
module main (
  input  a,
  input  b,
  output sum,
  output carry
);

  xor XOR (sum, a, b);
  and AND (carry, a, b);
endmodule
