// Logisim project XOR.circ as structural Verilog: 1 circuit, main circuit main
module main (
  input  in_1,
  input  in_2,
  output out_3
);

  wire AND_2_out, AND_out, Not_2_out, Not_out;

  not Not (Not_out, in_2);
  not Not_2 (Not_2_out, in_1);
  nand AND (AND_out, in_1, Not_out);
  nand AND_2 (AND_2_out, Not_2_out, in_2);
  or Or (out_3, AND_out, AND_2_out);
endmodule
