// Logisim project aAlu.circ as structural Verilog: 1 circuit, main circuit ALU
module ALU (
  input  [15:0] x,
  input  no,
  input  f,
  input  ny,
  input  zy,
  input  [15:0] y,
  input  nx,
  input  zx,
  output [15:0] out,
  output zr,
  output ng
);

  wire [15:0] add16_1_p3, and_1_out, multiplexer_1_out, multiplexer_2_out, multiplexer_3_out,
       multiplexer_4_out, multiplexer_6_out, not_1_out, not_2_out, not_3_out;

  Multiplexer #(.width(16), .enable("false")) multiplexer_1 (
    .in0(x), .in1({16{1'b0}}), .out(multiplexer_1_out), .sel(zx));
  Multiplexer #(.width(16), .enable("false")) multiplexer_2 (
    .in0(y), .in1({16{1'b0}}), .out(multiplexer_2_out), .sel(zy));
  Comparator #(.width(16)) comparator_1 (.a(out), .b({16{1'b0}}), .eq(zr), .lt(ng));  // open: gt
  Multiplexer #(.width(16), .enable("false")) multiplexer_3 (
    .in0(multiplexer_1_out), .in1(not_1_out), .out(multiplexer_3_out), .sel(nx));
  assign not_1_out = ~multiplexer_1_out;  // NOT_Gate not_1, 16 bits wide
  Multiplexer #(.width(16), .enable("false")) multiplexer_4 (
    .in0(multiplexer_2_out), .in1(not_2_out), .out(multiplexer_4_out), .sel(ny));
  assign not_2_out = ~multiplexer_2_out;  // NOT_Gate not_2, 16 bits wide
  assign and_1_out = multiplexer_3_out & multiplexer_4_out;  // AND_Gate and_1, 16 bits wide
  Multiplexer #(.width(16), .enable("false")) multiplexer_5 (
    .in0(multiplexer_6_out), .in1(not_3_out), .out(out), .sel(no));
  assign not_3_out = ~multiplexer_6_out;  // NOT_Gate not_3, 16 bits wide
  // Add16 add16_1: pin names not known; wires that end beside it: multiplexer_3_out, multiplexer_4_out, add16_1_p3
  Multiplexer #(.width(16), .enable("false")) multiplexer_6 (
    .in0(and_1_out), .in1(add16_1_p3), .out(multiplexer_6_out), .sel(f));
endmodule
